# Fritzing sketch Schematic_Circut (saved by Fritzing 0.9.4)
breadboards: 1

parts:
  R1 = Resistor [tolerance=±5% resistance=150 package=THT]
  LED2 = LED - 5mm [color="Green (555nm)" package="5 mm [THT]"]
  R2 = Resistor [tolerance=±5% resistance=150 package=THT]
  LED3 = LED - 5mm [color="Green (555nm)" package="5 mm [THT]"]
  R3 = Resistor [tolerance=±5% resistance=150 package=THT]
  LED1 = LED - 5mm [color="Green (555nm)" package="5 mm [THT]"]
  Blink!_Schematic = Arduino Uno (Rev3)

nets (from the breadboard view):
  N1: R1.Pin_0, Blink!_Schematic.D13/SCK
  N2: R1.Pin_1, LED1.cathode
  N3: LED2.cathode, R2.Pin_1
  N4: LED2.anode, LED3.anode, LED1.anode, Blink!_Schematic.GND
  N5: R2.Pin_0, Blink!_Schematic.D12/MISO
  N6: LED3.cathode, R3.Pin_1
  N7: R3.Pin_0, Blink!_Schematic.D11_PWM/MOSI
