# Fritzing sketch Fade-Schematic (saved by Fritzing 0.9.4)
breadboards: 1

parts:
  Part1 = Arduino Uno (Rev3)
  part = LED - 5mm [color="Green (555nm)" package="5 mm [THT]"]
  part_2 = LED - 5mm [color="Blue (430nm)" package="5 mm [THT]"]
  part_3 = LED - 5mm [color="Red (633nm)" package="5 mm [THT]"]
  part_4 = LED - 5mm [color="Yellow (585nm)" package="5 mm [THT]"]
  part_5 = Resistor [tolerance=±5% resistance=220 package=THT]
  Switch = Pushbutton [package="[THT]"]
  part_6 = Resistor [tolerance=±5% resistance=220 package=THT]
  part_7 = Resistor [tolerance=±5% resistance=220 package=THT]
  part_8 = Resistor [tolerance=±5% resistance=220 package=THT]
  part_9 = Resistor [tolerance=±5% resistance=220 package=THT]

nets (from the schematic view):
  N1: Part1.D9_PWM, part_3.anode
  N2: Part1.D10_PWM/SS, part_2.anode
  N3: Part1.D11_PWM/MOSI, part.anode
  N4: Part1.D2, Switch.Pin_3, Switch.Pin_4, part_9.Pin_0
  N5: Part1.D6_PWM, part_4.anode
  N6: Part1.5V, Switch.Pin_1, Switch.Pin_2
  N7: Part1.GND, part_5.Pin_0, part_6.Pin_0, part_7.Pin_0, part_8.Pin_0, part_9.Pin_1
  N8: part.cathode, part_5.Pin_1
  N9: part_2.cathode, part_6.Pin_1
  N10: part_3.cathode, part_7.Pin_1
  N11: part_4.cathode, part_8.Pin_1
